# Fritzing sketch Garduino_Schematic (saved by Fritzing 0.9.8b)
breadboards: 1

parts:
  Part1 = Arduino Uno (Rev3)
  Part2 = Soil Moisture Sensor
  Part3 = MAX7219 8x8 LedMatrix Module [part_number=DISPLAY]
  Tranzistor_Senzor = NPN-Transistor [package="TO92 [THT]"]
  M1 = DC Motor
  D1 = Rectifier Diode [part_number=1N4001 package="300 mil [THT]"]
  R3 = Resistor [tolerance=±5% power=0.25 resistance=100k package=THT]
  R5 = Resistor [tolerance=±5% power=0.25W resistance=330 package=THT]
  Q3 = NPN-Transistor [package="TO92 [THT]"]
  R6 = Resistor [tolerance=±5% power=0.25 resistance=100k package=THT]
  R7 = Resistor [tolerance=±5% power=0.25 resistance=330 package=THT]
  S1 = Toggle Switch [package=THT]

nets:
  N1: Part1.D11_PWM/MOSI, Part3.CS
  N2: Part1.D12/MISO, Part3.DIN
  N3: Part1.D13/SCK, Part3.CLK
  GND: Part1.GND, Part3.GND, M1.pin_2, D1.anode, R3.Pin_1, R6.Pin_1
  N4: Part1.D3_PWM, R7.Pin_1
  N5: Part1.D5_PWM, Part2.SIG
  N6: Part1.D6_PWM, R5.Pin_1
  N7: Part1.5V, Tranzistor_Senzor.C, Q3.C, S1.COM
  N8: Part2.VCC, Tranzistor_Senzor.E
  N9: Part3.VCC, S1.L1
  N10: Tranzistor_Senzor.B, R3.Pin_0, R5.Pin_0
  N11: D1.cathode, Q3.E
  N12: Q3.B, R6.Pin_0, R7.Pin_0

notes:
  Pompa de apa

custom parts:
  MAX7219 8x8 LedMatrix Module: Description: MAX7219 8x8 LedMatrix Red Module Dimensions: 32x32mm Documents:
